# Fritzing sketch receiver (saved by Fritzing 0.9.5d)

parts:
  A1 = wt32-eth01
  Power_5_5x2_1 = Power 5.5x2.5
  A2 = NRF24L01-BO-with-pcb [package=THT]

nets:
  GND: A1.Pin_2, A1.Pin_23, Power_5_5x2_1.GND, A2.GND
  N1: A1.Pin_12, Power_5_5x2_1.PWR, A2.VCC
  N2: A1.Pin_15, A2.M1
  N3: A1.Pin_16, A2.M0
  N4: A1.Pin_18, A2.SCK
  N5: A1.Pin_19, A2.CSN
  N6: A1.Pin_20, A2.CE

custom parts:
  wt32-eth01: WT32-ETH01 is an embedded serial port to Ethernet module based on ESP32 series designed by Wireless-Tag.
  NRF24L01-BO-with-pcb: NRF24L01-BO breakout board for the NRF24L01. Pcb view included.
