# Fritzing sketch relay_module (saved by Fritzing 0.9.5d)

parts:
  A1 = wt32-eth01
  8_Channel_Relay = 8 Channel Power Relay
  Power_5_5x2_1_5V = Power 5.5x2.5

nets:
  GND: A1.Pin_2, A1.Pin_23, 8_Channel_Relay.GND, Power_5_5x2_1_5V.GND
  N1: A1.Pin_12, 8_Channel_Relay.VCC, Power_5_5x2_1_5V.PWR
  N2: A1.Pin_15, 8_Channel_Relay.IN8
  N3: A1.Pin_16, 8_Channel_Relay.IN7
  N4: A1.Pin_17, 8_Channel_Relay.IN6
  N5: A1.Pin_18, 8_Channel_Relay.IN5
  N6: A1.Pin_19, 8_Channel_Relay.IN4
  N7: A1.Pin_20, 8_Channel_Relay.IN3

custom parts:
  wt32-eth01: WT32-ETH01 is an embedded serial port to Ethernet module based on ESP32 series designed by Wireless-Tag.
  8 Channel Power Relay: An 8 channel power relay. The module operates at 5V.
